# Fritzing sketch blu-clear_briefcase (saved by Fritzing 0.9.10b)
breadboards: 1

parts:
  Part1 = Adafruit Feather 32u4 Bluefruit [part_number="Adafruit #2829"]
  Part2 = NeoPixel NeoMatrix 8x8 [part_number=1487]
  Part4 = NeoPixel NeoMatrix 8x8 [part_number=1487]
  Part5 = NeoPixel NeoMatrix 8x8 [part_number=1487]  # not connected
  Part6 = NeoPixel NeoMatrix 8x8 [part_number=1487]
  Part7 = NeoPixel NeoMatrix 8x8 [part_number=1487]  # not connected
  Part8 = NeoPixel NeoMatrix 8x8 [part_number=1487]
  Part9 = NeoPixel NeoMatrix 8x8 [part_number=1487]  # not connected
  Part10 = NeoPixel NeoMatrix 8x8 [part_number=1487]
  Part11 = NeoPixel NeoMatrix 8x8 [part_number=1487]
  Part12 = NeoPixel NeoMatrix 8x8 [part_number=1487]
  Part13 = NeoPixel NeoMatrix 8x8 [part_number=1487]  # not connected
  Part14 = NeoPixel NeoMatrix 8x8 [part_number=1487]
  M1 = RioRand LM2596
  M4 = RioRand LM2596
  M5 = RioRand LM2596
  M6 = RioRand LM2596
  U1 = LIPO-2000mAh [package=lipo-2000]
  S2 = Reed switch [package=THT]
  S3 = Toggle Switch [package=THT]

nets:
  GND: Part1.GND, Part12.GND, M6.Pin_3, S2.pin_1
  N1: Part1.VBUS, Part12.VDD, M6.Pin_4
  N2: Part1.12, Part12.OUT
  N3: Part1.10, S2.pin_2
  N4: Part2.IN, Part11.GND
  VDD: Part2.VDD, Part11.VDD
  N5: Part2.GND, Part11.OUT
  VDD_2: Part4.VDD, Part8.VDD
  N6: Part4.OUT, Part8.IN
  GND_2: Part4.GND, Part8.GND
  N7: Part6.VDD, M1.Pin_3
  N8: Part6.GND, M1.Pin_4
  N9: Part10.VDD, M5.Pin_3
  N10: Part10.GND, M5.Pin_4
  N11: Part14.VDD, M4.Pin_3
  N12: Part14.GND, M4.Pin_4
  N13: M1.Pin_1, M4.Pin_1, M5.Pin_1, M6.Pin_1, S3.L1
  N14: M1.Pin_2, M4.Pin_2, M5.Pin_2, M6.Pin_2, U1.-
  N15: U1.+, S3.COM, S3.L2

notes:
  5000 mAh 2S7.4 LiPo
  Open lid detector
  5V 3A Buck Converter

custom parts:
  Adafruit Feather 32u4 Bluefruit: This is the Adafruit Feather 32u4 Bluefruit - our take on an 'all-in-one' Arduino-compatible + Bluetooth Low Energy with built in USB and battery charging. Its an Adafruit Feather 32u4 with a BTLE module, ready to rock! We have other boards in the Feather family, check'em out here. Bluetooth Low Energy is the hottest new low-power, 2.4GHz spectrum wireless protocol. In particular, its the only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
  NeoPixel NeoMatrix 8x8: Put on your sunglasses before wiring up this LED matrix - 64 eye-blistering RGB LEDs adorn the NeoMatrix for a blast of configurable color. Arranged in an 8x8 matrix, each pixel is individually addressable. Only one microcontroller pin is required to control all the LEDs, and you get 24 bit color for each LED.
